// Logisim project Assignment no 2.circ as structural Verilog: 1 circuit, main circuit main
module main (
  input  D6,
  input  S0,
  input  S1,
  input  S2,
  input  D7,
  input  D5,
  input  D0,
  input  D1,
  input  D4,
  input  D3,
  input  D2,
  output out_12
);

  wire AND_2_out, AND_3_out, AND_4_out, AND_5_out, AND_6_out, AND_7_out, AND_8_out, AND_out, not_1_out,
       not_2_out, not_3_out;

  and AND (AND_out, not_1_out, not_2_out, not_3_out, D0);
  not not_1 (not_1_out, S0);
  and AND_2 (AND_2_out, not_1_out, not_2_out, S2, D1);
  not not_2 (not_2_out, S1);
  and AND_3 (AND_3_out, not_1_out, S1, not_3_out, D2);
  not not_3 (not_3_out, S2);
  and AND_4 (AND_4_out, not_1_out, S1, S2, D3);
  and AND_5 (AND_5_out, S0, not_2_out, not_3_out, D4);
  and AND_6 (AND_6_out, S0, not_2_out, S2, D5);
  and AND_7 (AND_7_out, S0, S1, not_3_out, D6);
  and AND_8 (AND_8_out, S0, S1, S2, D7);
  or OR (out_12, AND_7_out, AND_8_out, AND_6_out, AND_5_out, AND_4_out, AND_3_out, AND_2_out, AND_out);
endmodule
