// Logisim project assignment 2.circ as structural Verilog: 1 circuit, main circuit main
module main (
  input  Q,
  input  S0,
  input  Q_2,
  input  S1,
  input  Q_3,
  input  S2,
  input  Q_4,
  input  Q_5,
  input  in_9,
  input  Q_6,
  input  in_11,
  output Y0,
  output Y1,
  output Y2,
  output Y3,
  output Y4,
  output Y5,
  output Y6,
  output Y7
);

  wire not_1_out, not_2_out, not_3_out;

  not not_1 (not_1_out, S0);
  not not_2 (not_2_out, S1);
  not not_3 (not_3_out, S2);
  and AND (Y6, S0, S1, not_3_out, Q_6);
  and AND_2 (Y7, S0, S1, S2, in_11);
  and AND_3 (Y0, not_1_out, not_2_out, not_3_out, Q);
  and AND_4 (Y3, not_1_out, S1, S2, Q_4);
  and AND_5 (Y1, not_1_out, not_2_out, S2, Q_2);
  and AND_6 (Y2, not_1_out, S1, not_3_out, Q_3);
  and AND_7 (Y4, S0, S1, not_3_out, Q_5);
  and AND_8 (Y5, S0, not_2_out, S2, in_9);

  // Notes on the sheet:
  //   1*8 Demux
endmodule
