// Logisim project First 6 Gates Lab 3.circ as structural Verilog: 1 circuit, main circuit main
module main (
  input  A,
  input  B,
  input  A_2,
  input  B_2,
  input  A_3,
  input  A_4,
  input  B_3,
  input  A_5,
  input  B_4,
  input  A_6,
  input  B_5,
  input  A_7,
  input  B_6,
  output Y,
  output Y_2,
  output out_16,
  output A_B__prime,
  output A_B__prime_2,
  output A_prime_B_AB_prime,
  output A_prime_B_AB_prime__prime
);

  wire AND_2_out, AND_3_out, AND_4_out, AND_5_out, AND_6_out, NOT_2_out, NOT_3_out, NOT_4_out, NOT_5_out,
       OR_2_out, OR_4_out;

  and AND (Y, A, B);
  or OR (Y_2, A_2, B_2);
  not NOT (out_16, A_3);
  and AND_2 (AND_2_out, A_4, B_3);
  or OR_2 (OR_2_out, A_5, B_4);
  not NOT_2 (NOT_2_out, A_6);
  not NOT_3 (NOT_3_out, B_5);
  not NOT_4 (NOT_4_out, A_7);
  not NOT_5 (NOT_5_out, B_6);
  not NOT_6 (A_B__prime, AND_2_out);
  not NOT_7 (A_B__prime_2, OR_2_out);
  and AND_3 (AND_3_out, NOT_2_out, B_5);
  and AND_4 (AND_4_out, A_6, NOT_3_out);
  and AND_5 (AND_5_out, NOT_4_out, B_6);
  and AND_6 (AND_6_out, A_7, NOT_5_out);
  or OR_3 (A_prime_B_AB_prime, AND_3_out, AND_4_out);
  or OR_4 (OR_4_out, AND_5_out, AND_6_out);
  not not_8 (A_prime_B_AB_prime__prime, OR_4_out);

  // Notes on the sheet:
  //   (A*B)
  //   A+B
  //   NAND
  //   NOR
  //   A'
  //   B'
  //   A'
  //   B'
  //   A'B
  //   B'A
  //   A'B+AB'
  //   AND
  //   OR
  //   NOT
  //   NAND
  //   NOR
  //   XOR
  //   XNOR
endmodule
