// Logisim project Lab4 Task1 1st.circ as structural Verilog: 1 circuit, main circuit main
module main (
  input  A,
  input  B,
  input  C,
  input  A_2,
  input  B_2,
  input  C_2,
  output F,
  output F1
);

  wire A_prime_out, AND_2_out, AND_3_out, AND_4_out, AND_5_out, AND_out, B_prime_out, not_1_out, not_2_out;

  not A_prime (A_prime_out, A);
  not B_prime (B_prime_out, B);
  not not_1 (not_1_out, A_2);
  not not_2 (not_2_out, B_2);
  and AND (AND_out, A_prime_out, B_prime_out, C);
  and AND_2 (AND_2_out, A, B_prime_out);
  and AND_3 (AND_3_out, not_1_out, C_2);
  and AND_4 (AND_4_out, A_prime_out, B, C);
  and AND_5 (AND_5_out, A_2, not_2_out);
  or OR (F, AND_out, AND_4_out, AND_2_out);
  or OR_2 (F1, AND_3_out, AND_5_out);

  // Notes on the sheet:
  //   A'
  //   B'
  //   A'B'C
  //   AB'
  //   A'C
  //   A'BC
  //   AB'
  //   A'B'C+A'BC+AB'=F
  //   A'C+AB'=F1
endmodule
