// Logisim project Lab4 Task1 Lab task.circ as structural Verilog: 1 circuit, main circuit main
module main (
  input  A,
  input  B,
  input  C,
  input  A_2,
  input  B_2,
  input  C_2,
  input  X,
  input  Y,
  input  Z,
  input  X_2,
  input  Z_2,
  output F,
  output F1,
  output F_2,
  output F2
);

  wire A_prime_out, AND_2_out, AND_4_out, AND_5_out, AND_6_out, AND_7_out, AND_8_out, AND_out, B_prime_out,
       not_1_out, not_2_out, not_3_out;

  not A_prime (A_prime_out, A);
  not B_prime (B_prime_out, B);
  not not_1 (not_1_out, A_2);
  not not_2 (not_2_out, B_2);
  not not_3 (not_3_out, Y);
  and AND (AND_out, A_prime_out, B_prime_out, C);
  and AND_2 (AND_2_out, X, Y, Z);
  and AND_3 (F2, X_2, Z_2);
  and AND_4 (AND_4_out, A, B_prime_out);
  and AND_5 (AND_5_out, not_1_out, C_2);
  and AND_6 (AND_6_out, A_prime_out, B, C);
  and AND_7 (AND_7_out, A_2, not_2_out);
  and AND_8 (AND_8_out, X, not_3_out, Z);
  or OR (F, AND_out, AND_6_out, AND_4_out);
  or OR_2 (F1, AND_5_out, AND_7_out);
  or OR_3 (F_2, AND_2_out, AND_8_out, AND_2_out);

  // Notes on the sheet:
  //   A'
  //   B'
  //   XZ=F2
  //                                              Task 1 before simplification
  //   A'B'C
  //   AB'
  //   A'C
  //   XYZ
  //   XY'Z
  //   A'BC
  //   Task 1 After Simplification
  //   AB'
  //   A'B'C+A'BC+AB'=F
  //   A'C+AB'=F1
  //   Task 2 Before Simplification
  //   XYZ+XY'Z+XYZ=F
  //   Task 2 After Simplification
endmodule
