// Logisim project review question.circ as structural Verilog: 1 circuit, main circuit main
module main (
  input  X,
  input  Y,
  input  Z,
  output A_B_C_F_prime
);

  wire OR_2_out, OR_3_out, OR_out, X_prime_out, Y_prime_out, Z_prime_out;

  not X_prime (X_prime_out, X);
  not Y_prime (Y_prime_out, Y);
  not Z_prime (Z_prime_out, Z);
  or OR (OR_out, Y, X_prime_out, Z_prime_out);
  or OR_2 (OR_2_out, Y, Z, X_prime_out);
  or OR_3 (OR_3_out, X, Y_prime_out);
  and AND (A_B_C_F_prime, OR_out, OR_3_out, OR_2_out);

  // Notes on the sheet:
  //   X'+Y+Z'=A
  //   X+Y'=B
  //   X'+Y+Z=C
endmodule
