// Logisim project TASK 1.circ as structural Verilog: 1 circuit, main circuit main
module main (
  input  I1,
  input  i1_2,
  input  I2,
  input  I1_3,
  input  I2_2,
  output Y1,
  output Y1_2,
  output Y1_3
);

  not NOT (Y1, I1);
  and AND (Y1_2, i1_2, I2);
  or OR (Y1_3, I1_3, I2_2);

  // Notes on the sheet:
  //   I1'=Y1
  //   I1.I2=Y1
  //   I1+I2=Y1
endmodule
