// Logisim project Experiment no 9.circ as structural Verilog: 1 circuit, main circuit main
module main (
  input  A1,
  input  A2,
  input  B1,
  input  B2,
  output out_5,
  output out_6,
  output out_7
);

  wire AND_2_out, AND_3_out, AND_4_out, AND_5_out, AND_6_out, AND_7_out, AND_8_out, AND_9_out, AND_10_out,
       AND_out, not_1_out, not_2_out, not_3_out, not_4_out, not_5_out;

  not not_1 (not_1_out, A1);
  not not_2 (not_2_out, A2);
  not not_3 (not_3_out, B1);
  not not_4 (not_4_out, B2);
  not not_5 (not_5_out, B2);
  and AND (AND_out, not_1_out, B1);
  and AND_2 (AND_2_out, not_1_out, not_2_out, B2);
  and AND_3 (AND_3_out, not_2_out, B1, B2);
  and AND_4 (AND_4_out, A1, not_3_out);
  and AND_5 (AND_5_out, not_4_out, A2, A1);
  and AND_6 (AND_6_out, A2, not_3_out, not_5_out);
  and AND_7 (AND_7_out, not_5_out, not_3_out, not_2_out, not_1_out);
  or OR (out_6, AND_out, AND_2_out, AND_3_out);
  and AND_8 (AND_8_out, not_1_out, A2, not_3_out, B2);
  and AND_9 (AND_9_out, B1, B2, A2, A1);
  or OR_2 (out_7, AND_4_out, AND_5_out, AND_6_out);
  and AND_10 (AND_10_out, not_2_out, A1, B1, not_5_out);
  or OR_3 (out_5, AND_7_out, AND_8_out, AND_9_out, AND_10_out);

  // Notes on the sheet:
  //   A2'
  //   For 2-bit comparator
  //   A1'
  //   B2'
  //   A1'B1
  //   B2B1A2'
  //   A1
  //   B1'
  //   A1'B2A2'
  //   A1B1'
  //   A1A2B2
  //   A2B1'B2'
  //   For Less 
  //   A1'B1+A1'B2A2'+B2B1A2'
  //   A1'A2'B1'B2'
  //   B1B2A2A1
  //   A1'A2B1'B2
  //   A2'A1B1B2'
  //   For Greater
  //   A1B1'+A1A2B2+A2B1'B2'
  //   For Equal
endmodule
