// Logisim project experimentno10.circ as structural Verilog: 1 circuit, main circuit main
module main (
  input  A,
  input  X,
  input  B,
  input  Y,
  input  C,
  input  A_2,
  input  B_2,
  input  A_3,
  input  Cin,
  input  B_3,
  input  A_4,
  input  A_5,
  input  B_4,
  input  B_5,
  input  C_2,
  input  C_3,
  output sum,
  output carry,
  output out_19,
  output out_20,
  output A_prime_B_AB_prime,
  output CARRY_2,
  output A_prime_B,
  output Difference,
  output Borrow
);

  wire AND_2_out, AND_3_out, AND_4_out, AND_5_out, AND_7_out, AND_8_out, AND_9_out, AND_out, not_1_out,
       not_2_out, OR_out, XOR_2_out, XOR_7_out, XOR_out;

  xor XOR (XOR_out, A_5, B_5);
  not not_1 (not_1_out, A_5);
  xor XOR_2 (XOR_2_out, A_2, B_2);
  and AND (AND_out, A_2, B_2);
  xor XOR_3 (Difference, XOR_out, C_3);
  and AND_2 (AND_2_out, not_1_out, B_5);
  and AND_3 (AND_3_out, not_1_out, C_3);
  and AND_4 (AND_4_out, B_5, C_3);
  xor XOR_4 (sum, X, Y);
  xor XOR_5 (out_20, XOR_2_out, Cin);
  and AND_5 (AND_5_out, XOR_2_out, Cin);
  or OR (OR_out, AND_2_out, AND_3_out);
  and AND_6 (carry, X, Y);
  or OR_2 (CARRY_2, AND_5_out, AND_out);
  or OR_3 (Borrow, OR_out, AND_4_out);
  and AND_7 (AND_7_out, A, C);
  and AND_8 (AND_8_out, B, C);
  and AND_9 (AND_9_out, A, B);
  xor xor_6 (A_prime_B_AB_prime, A_3, B_3);
  not not_2 (not_2_out, A_3);
  // NOT_Gate not_3 has open pins: in=A_4, out=open
  // NOT_Gate not_4 has open pins: in=B_4, out=open
  // NOT_Gate not_5 has open pins: in=C_2, out=open
  xor XOR_7 (XOR_7_out, AND_7_out, AND_8_out);
  and and_10 (A_prime_B, not_2_out, B_3);
  or OR_4 (out_19, XOR_7_out, AND_9_out);

  // Notes on the sheet:
  //   Half Adder
  //   Full Adder
  //   A
  //   B
  //   A'
  //   B
  //   A'
  //   C
  //   B
  //   C
  //   A'B+AB'
  //   Cin
  //   Full Subtractor
  //   SUM
  //   A
  //   C
  //   B
  //   C
  //   A
  //   B
  //   Half Subtractor
  //   A'
  //   B
  //   Difference
  //   Borrow
  //   Cout  For Full Adder
endmodule
