// Logisim project Experiment bo 12.circ as structural Verilog: 1 circuit, main circuit main
module main (
  input  A,
  input  B,
  input  D0,
  input  D1,
  input  D2,
  input  D3,
  input  A_2,
  input  B_2,
  input  E,
  output out_10,
  output out_11,
  output out_12,
  output out_13,
  output A_3,
  output B_3,
  output out_16,
  output out_17,
  output out_18,
  output out_19,
  output out_20,
  output out_21,
  output out_22,
  output out_23
);

  wire AND_5_out, AND_6_out, AND_7_out, AND_8_out, not_1_out, not_2_out, not_3_out, not_4_out, not_5_out,
       not_6_out, not_7_out, not_8_out, not_9_out;

  not not_1 (not_1_out, A);
  not not_2 (not_2_out, B);
  not not_3 (not_3_out, D0);
  not not_4 (not_4_out, D1);
  not not_5 (not_5_out, A_2);
  and AND (out_10, not_1_out, not_2_out);
  and AND_2 (out_11, not_1_out, B);
  and AND_3 (out_12, not_2_out, A);
  and AND_4 (out_13, A, B);
  not not_6 (not_6_out, D2);
  not not_7 (not_7_out, D3);
  not not_8 (not_8_out, B_2);
  not not_9 (not_9_out, E);
  and AND_5 (AND_5_out, not_7_out, D2, not_4_out, not_3_out);
  and AND_6 (AND_6_out, not_3_out, not_4_out, not_6_out, D3);
  and AND_7 (AND_7_out, not_3_out, D1, not_6_out, not_7_out);
  and AND_8 (AND_8_out, not_3_out, not_4_out, not_6_out, D3);
  and AND_9 (out_16, not_5_out, not_8_out, not_9_out);
  and AND_10 (out_17, not_5_out, B_2, not_9_out);
  and AND_11 (out_18, A_2, not_8_out, not_9_out);
  and AND_12 (out_19, A_2, B_2, not_9_out);
  and AND_13 (out_20, not_5_out, not_8_out, E);
  and AND_14 (out_21, not_5_out, B_2, E);
  and AND_15 (out_22, A_2, not_8_out, E);
  and AND_16 (out_23, A_2, B_2, E);
  or OR (A_3, AND_5_out, AND_6_out);
  or OR_2 (B_3, AND_7_out, AND_8_out);

  // Notes on the sheet:
  //   A
  //   B
  //   Decoder 2*4
  //   A'
  //   B'
  //   A'
  //   B
  //   B'
  //   A
  //   A
  //   B
  //   Encoder 4*2
  //   Experiment no 12
  //   D0
  //   D1
  //   D2
  //   D3
  //   D4
  //   D5
  //   D6
  //   D7
endmodule
