// Logisim project Function of F1.circ as structural Verilog: 1 circuit, main circuit main
module main (
  input  X,
  input  Y,
  input  Z,
  input  Z_2,
  input  X_2,
  input  Y_2,
  input  Z_3,
  input  X_3,
  input  Y_3,
  input  Z_4,
  output out_11,
  output out_12,
  output G1_G2_G3_F2,
  output X_prime_YZ_XY_prime_F2
);

  wire AND_2_out, AND_3_out, AND_4_out, AND_5_out, AND_6_out, AND_7_out, AND_8_out, AND_9_out, AND_out,
       not_1_out, not_2_out, not_3_out, not_4_out, not_5_out, not_6_out, not_7_out;

  not not_1 (not_1_out, X);
  not not_2 (not_2_out, Y);
  buf buffer (out_12, Z_2);
  not not_3 (not_3_out, X_2);
  not not_4 (not_4_out, Y_2);
  not not_5 (not_5_out, Z_3);
  not not_6 (not_6_out, X_3);
  not not_7 (not_7_out, Y_3);
  and AND (AND_out, not_1_out, not_2_out, Z);
  and AND_2 (AND_2_out, not_1_out, Y, Z);
  and AND_3 (AND_3_out, X, not_2_out, Z);
  and AND_4 (AND_4_out, not_6_out, Y_3, Z_4);
  and AND_5 (AND_5_out, X_3, not_7_out);
  and AND_6 (AND_6_out, Z_3, Y_2, not_3_out);
  and AND_7 (AND_7_out, X_2, not_4_out, not_5_out);
  and AND_8 (AND_8_out, X_2, not_4_out, Z_3);
  and AND_9 (AND_9_out, Z, Y, X);
  or OR (X_prime_YZ_XY_prime_F2, AND_4_out, AND_5_out);
  or OR_2 (G1_G2_G3_F2, AND_6_out, AND_7_out, AND_8_out);
  or OR_3 (out_11, AND_9_out, AND_out, AND_2_out, AND_3_out);

  // Notes on the sheet:
  //   Simplified Function of F1
  //   X'
  //   Y'
  //   FOR FUNCTION F1
  //   X'.Y'.Z=T1
  //   X'.Y.Z=T2
  //   FOR FUNCTION F2
  //   Simplified Function Of F2
  //   X.Y'Z=T3
  //   X'YZ=G1
  //   XY'Z'=G2
  //   XY'Z=G3
  //   X'YZ
  //   XY'
  //   XYZ=T4
  //   T1+T2+T3+T4=F1
endmodule
