// Logisim project lab manual.circ as structural Verilog: 1 circuit, main circuit main
module main (
  input  A,
  input  B,
  input  C,
  input  D,
  output out_5
);

  wire AND_2_out, AND_3_out, AND_out, not_1_out, not_2_out;

  not not_1 (not_1_out, A);
  not not_2 (not_2_out, B);
  and AND (AND_out, A, B);
  and AND_2 (AND_2_out, not_1_out, B, C);
  and AND_3 (AND_3_out, not_2_out, C, D);
  or OR (out_5, AND_out, AND_2_out, AND_3_out);

  // Notes on the sheet:
  //   AFTER SIMPLIFICATION
  //   AB
  //   A'BC
  //   B'CD
endmodule
