// Logisim project LAbTask.circ as structural Verilog: 1 circuit, main circuit main
module main (
  input  A,
  input  B,
  input  A_2,
  input  B_2,
  input  A_3,
  input  B_3,
  input  A_4,
  input  B_4,
  output A_prime_B_prime_AB_F,
  output A_prime_B_prime_AB_F_2,
  output out_11,
  output A_prime_B_AB_prime_F
);

  wire NAND_2_out, NAND_3_out, NAND_4_out, NAND_5_out, NAND_6_out, NAND_7_out, NAND_8_out, NAND_out,
       NOR_2_out, NOR_3_out, nor_4_out, NOR_5_out, NOR_6_out, NOR_7_out, NOR_8_out, NOR_9_out, NOR_10_out,
       NOR_out;

  nor NOR (NOR_out, B_3, B_3);
  nand NAND (NAND_out, A, A);
  nand NAND_2 (NAND_2_out, B, B);
  nor NOR_2 (NOR_2_out, A_2, B_2);
  nor NOR_3 (NOR_3_out, B_2, B_2);
  nor nor_4 (nor_4_out, A_3, A_3);
  nand NAND_3 (NAND_3_out, A_4, A_4);
  nand NAND_4 (NAND_4_out, B_4, B_4);
  nand NAND_5 (NAND_5_out, NAND_out, NAND_2_out);
  nand NAND_6 (NAND_6_out, A, B);
  nor NOR_5 (NOR_5_out, A_2, A_2);
  nor NOR_6 (NOR_6_out, A_3, NOR_out);
  nor NOR_7 (NOR_7_out, nor_4_out, B_3);
  nand NAND_7 (NAND_7_out, NAND_3_out, B_4);
  nand NAND_8 (NAND_8_out, NAND_4_out, A_4);
  nor NOR_8 (NOR_8_out, NOR_5_out, NOR_3_out);
  nand NAND_9 (A_prime_B_prime_AB_F, NAND_5_out, NAND_6_out);
  nor NOR_9 (NOR_9_out, NOR_6_out, NOR_7_out);
  nand NAND_10 (A_prime_B_AB_prime_F, NAND_7_out, NAND_8_out);
  nor NOR_10 (NOR_10_out, NOR_2_out, NOR_8_out);
  nor NOR_11 (out_11, NOR_9_out, NOR_9_out);
  nor NOR_12 (A_prime_B_prime_AB_F_2, NOR_10_out, NOR_10_out);

  // Notes on the sheet:
  //   B'
  //   A'
  //   B'
  //   XNOR using NOR Gate
  //   XOR using NOR
  //   A'
  //   XOR Using NAND
  //   A'
  //   B'
  //   XNOR using Nand Gate 
  //   A'B'
  //   AB
  //   A'B
  //   AB'
  //   XNOR=A'B'+AB
  //   A'B'
  //   AB
  //   XOR=A'B+AB'
  //   XOR=A'B+AB'
  //   XOR=A'B+AB'
  //   AB'
  //   A'B
  //   XNOR=A'B'+AB
endmodule
