// Logisim project review questions.circ as structural Verilog: 1 circuit, main circuit main
module main (
  input  X,
  input  Y,
  input  Z,
  input  X_2,
  input  Y_2,
  input  Z_2,
  output F_XY_XY_prime_Z_XYZ,
  output out_8
);

  wire NAND_2_out, NAND_3_out, NAND_4_out, NAND_out, nor_1_out, nor_2_out, nor_3_out, nor_4_out, nor_5_out,
       nor_6_out, nor_7_out;

  nand NAND (NAND_out, Y, Y);
  nor nor_1 (nor_1_out, X_2, Y_2, Z_2);
  nor nor_2 (nor_2_out, Y_2, Y_2);
  nor nor_3 (nor_3_out, Z_2, Z_2);
  nand NAND_2 (NAND_2_out, X, Y);
  nor nor_4 (nor_4_out, nor_1_out, nor_1_out);
  nand NAND_3 (NAND_3_out, X, NAND_out, Z);
  nand NAND_4 (NAND_4_out, X, Y, Z);
  nor nor_5 (nor_5_out, nor_2_out, X_2, nor_3_out);
  nor nor_6 (nor_6_out, nor_4_out, nor_4_out);
  nor nor_7 (nor_7_out, nor_5_out, nor_5_out);
  nand NAND_5 (F_XY_XY_prime_Z_XYZ, NAND_2_out, NAND_3_out, NAND_4_out);
  nor nor_8 (out_8, nor_6_out, nor_7_out);

  // Notes on the sheet:
  //   Y'
  //   Y'
  //   Z'
  //   F=XY+XY'Z+XYZ
  //   XY
  //   X+Y+Z
  //   XY'Z
  //   XYZ
  //   X+Y'+Z'
  //   (X+Y+Z).(X+Y'+Z')
endmodule
