// Logisim project Lab7task1.circ as structural Verilog: 1 circuit, main circuit main
module main (
  input  X1,
  input  X2,
  input  X3,
  input  X4,
  input  X1_2,
  input  X2_2,
  input  X3_2,
  input  X4_2,
  input  B_prime,
  input  C_prime,
  output out_11,
  output out_12,
  output B_prime_C_prime
);

  wire AND_2_out, AND_3_out, AND_4_out, AND_5_out, AND_6_out, AND_7_out, AND_8_out, AND_9_out, AND_out,
       not_1_out, not_2_out, not_3_out, not_4_out, not_5_out, not_6_out, not_7_out, not_8_out, not_9_out,
       not_10_out;

  not not_1 (not_1_out, X1);
  not not_2 (not_2_out, X2);
  not not_3 (not_3_out, X3);
  not not_4 (not_4_out, X4);
  and AND (AND_out, X1_2, X2_2);
  not not_5 (not_5_out, X2_2);
  and AND_2 (AND_2_out, X3_2, X4_2);
  not not_6 (not_6_out, B_prime);
  not not_7 (not_7_out, C_prime);
  and AND_3 (AND_3_out, not_2_out, not_3_out);
  and AND_4 (AND_4_out, X3, X4);
  not not_8 (not_8_out, X1_2);
  and AND_5 (AND_5_out, not_5_out, X4_2);
  not not_9 (not_9_out, X3_2);
  not not_10 (not_10_out, X4_2);
  or OR (B_prime_C_prime, not_6_out, not_7_out);
  and AND_6 (AND_6_out, not_4_out, not_1_out, not_3_out);
  and AND_7 (AND_7_out, X1, not_2_out);
  and AND_8 (AND_8_out, X4, X1);
  and AND_9 (AND_9_out, not_8_out, not_9_out, not_10_out);
  or OR_2 (out_11, AND_6_out, AND_7_out, AND_3_out, AND_4_out, AND_8_out);
  or OR_3 (out_12, AND_out, AND_5_out, AND_2_out, AND_9_out);

  // Notes on the sheet:
  //   TASK 1
  //   X4'
  //   X1'
  //   X3'
  //   X4'
  //   X1.X2
  //   X2'
  //   X4
  //   X3.X4
  //   X1
  //   X2'
  //   X4
  //   X1
  //   TASK 1 Simplified Function
  //   X1'
  //   X3'
  //   X4'
  //   Simplified function
  //   X2'.X4
  //   X1'.X3'.X4'
  //   False
  //   TRUE
endmodule
