// Logisim project review questions.circ as structural Verilog: 1 circuit, main circuit main
module main (
  input  A,
  input  B,
  input  C,
  input  D,
  input  A_2,
  input  B_2,
  input  C_2,
  output out_8,
  output out_9
);

  wire AND_2_out, AND_3_out, AND_4_out, AND_5_out, AND_out, not_1_out, not_2_out, not_3_out;

  not not_1 (not_1_out, A);
  not not_2 (not_2_out, C);
  not not_3 (not_3_out, D);
  and AND (AND_out, C_2, A_2);
  and AND_2 (AND_2_out, B_2, C_2);
  and AND_3 (AND_3_out, not_1_out, not_3_out);
  and AND_4 (AND_4_out, B, not_3_out);
  and AND_5 (AND_5_out, A_2, B_2);
  or OR (out_8, AND_3_out, not_2_out, AND_4_out);
  or OR_2 (out_9, AND_out, AND_5_out, AND_2_out);

  // Notes on the sheet:
  //   Q No 1
  //   A'D'
  //   BD'
endmodule
