// Logisim project Experiment no 8.circ as structural Verilog: 1 circuit, main circuit main
module main (
  input  T1,
  input  T2,
  input  T3,
  input  T1_2,
  input  T2_2,
  input  T3_2,
  output out_7,
  output out_8
);

  wire AND_2_out, AND_3_out, AND_out, NAND_2_out, NAND_3_out, NAND_4_out, NAND_5_out, NAND_out, OR_out;

  and AND (AND_out, T3, T1);
  and AND_2 (AND_2_out, T2, T3);
  and AND_3 (AND_3_out, T1, T2);
  nand NAND (NAND_out, T3_2, T1_2);
  nand NAND_2 (NAND_2_out, T2_2, T3_2);
  nand NAND_3 (NAND_3_out, T1_2, T2_2);
  or OR (OR_out, AND_out, AND_2_out);
  nand NAND_4 (NAND_4_out, NAND_out, NAND_2_out);
  or OR_2 (out_7, OR_out, AND_3_out);
  nand NAND_5 (NAND_5_out, NAND_4_out, NAND_4_out);
  nand NAND_6 (out_8, NAND_5_out, NAND_3_out);

  // Notes on the sheet:
  //   T3
  //   T1
  //   T2
  //   T3
  //   T1
  //   T2
  //   T3
  //   T1
  //   T2
  //   T3
  //   T1
  //   T2
  //   LOGIC DIAGRAM WITH BASIC GATES
  //   Implement using Basic Gates
  //   Implement using NAND
  //   T3T1+T2T3
  //   Function=T1.T3+T2.T3+T1.T2
  //   T3T1+T2T3+T1T2
  //   After simplify NAND Gates
endmodule
