// Logisim project Q1.circ as structural Verilog: 1 circuit, main circuit main
module main (
  input  A,
  input  B,
  input  C,
  input  D,
  input  in_5,
  input  in_6,
  output out_7,
  output out_8
);

  wire nand_1_out, nand_2_out, nand_3_out, nand_4_out, nand_5_out, nand_6_out, nand_7_out, nand_8_out;

  nand nand_1 (nand_1_out, A, A);
  nand nand_2 (nand_2_out, B, B);
  nand nand_3 (nand_3_out, C, C);
  nand nand_4 (nand_4_out, in_5, in_6);
  nand nand_5 (nand_5_out, nand_1_out, nand_3_out);
  nand nand_6 (nand_6_out, nand_1_out, D);
  nand nand_7 (nand_7_out, nand_3_out, nand_2_out);
  nand nand_8 (nand_8_out, nand_2_out, D);
  nand nand_9 (out_8, nand_4_out, nand_4_out);
  nand nand_10 (out_7, nand_5_out, nand_6_out, nand_7_out, nand_8_out);

  // Notes on the sheet:
  //   A'C'
  //   A'D
  //   B'C'
  //   B'D
endmodule
